// Logisim project assignment1.circ as structural Verilog: 1 circuit, main circuit main
module main (
  input  ON_OFF,
  input  in_2,
  input  in_3
);

  wire and_1_out, and_2_out, and_3_out, and_4_out, and_5_out, and_10_out, and_11_out, and_12_out, and_13_out,
       and_14_out, and_15_out, and_16_out, and_17_out, and_18_out, and_19_out, and_20_out, and_21_out,
       and_22_out, and_23_out, and_24_out, and_25_out, and_26_out, and_27_out, and_28_out, and_29_out,
       and_30_out, and_31_out, and_32_out, and_33_out, and_34_out, and_35_out, and_36_out, and_37_out,
       and_38_out, and_39_out, and_40_out, and_41_out, and_46_out, and_47_out, and_48_out, and_49_out,
       and_50_out, and_51_out, and_52_out, and_53_out, and_54_out, and_55_out, and_56_out, and_57_out,
       and_58_out, and_59_out, and_60_out, and_61_out, and_62_out, and_63_out, and_64_out, button_1_out,
       button_2_out, button_3_out, button_4_out, button_5_out, button_6_out, d_ff_1_q, d_ff_2_q, d_ff_2_qn,
       d_ff_3_q, d_ff_4_q, d_ff_5_q, d_ff_5_qn, d_ff_6_q, d_ff_7_q, d_ff_8_q, d_ff_8_qn, d_ff_9_q, d_ff_10_q,
       d_ff_11_q, d_ff_11_qn, d_ff_12_q, d_ff_13_q, d_ff_14_q, d_ff_14_qn, d_ff_15_q, d_ff_15_qn, d_ff_16_q,
       d_ff_16_qn, d_ff_17_q, j_k_ff_1_q, j_k_ff_1_qn, nor_1_out, not_1_out, not_2_out, not_3_out, not_4_out,
       not_5_out, not_6_out, not_7_out, not_8_out, not_9_out, not_10_out, not_11_out, not_12_out, not_13_out,
       not_14_out, not_15_out, not_16_out, or_1_out, or_2_out, or_3_out, or_4_out, or_5_out, or_6_out,
       or_7_out, or_8_out, or_9_out, or_10_out, or_11_out, or_12_out, or_13_out, or_14_out, or_15_out,
       or_16_out, or_17_out, or_18_out, or_19_out, or_20_out, or_21_out, or_22_out, or_23_out, or_24_out,
       xnor_1_out, xor_1_out, xor_2_out, xor_3_out, xor_4_out, xor_5_out, xor_6_out, xor_7_out, xor_8_out;
  wire [3:0] and_6_out, and_42_out;

  Button button_1 (.out(button_1_out));
  Button button_2 (.out(button_2_out));
  and and_1 (and_1_out, button_1_out, ON_OFF);
  and and_2 (and_2_out, ON_OFF, button_2_out);
  D_Flip_Flop d_ff_1 (.D(and_2_out), .clk(and_2_out), .Q(d_ff_1_q), .reset(and_3_out));  // open: Qn, preset
  and and_3 (and_3_out, and_1_out, and_1_out);
  or or_1 (or_1_out, and_1_out, and_2_out);
  Hex_Digit_Display hex_digit_display_1 (.value(and_42_out));  // open: dp
  Hex_Digit_Display hex_digit_display_2 (.value(and_6_out));  // open: dp
  Button button_3 (.out(button_3_out));
  Button button_4 (.out(button_4_out));
  not not_1 (not_1_out, d_ff_1_q);
  and and_4 (and_4_out, button_3_out, ON_OFF);
  and and_5 (and_5_out, ON_OFF, button_4_out);
  and and_6 (and_6_out[0], ON_OFF, d_ff_2_q);
  and and_7 (and_6_out[1], ON_OFF, d_ff_5_q);
  and and_8 (and_6_out[2], ON_OFF, d_ff_8_q);
  and and_9 (and_6_out[3], ON_OFF, d_ff_11_q);
  or or_2 (or_2_out, d_ff_1_q, not_1_out);
  and and_10 (and_10_out, d_ff_1_q, nor_1_out);
  Button button_5 (.out(button_5_out));
  Button button_6 (.out(button_6_out));
  xor xor_1 (xor_1_out, or_2_out, d_ff_2_q);
  or or_3 (or_3_out, and_10_out, and_11_out);
  not not_2 (not_2_out, and_5_out);
  D_Flip_Flop d_ff_2 (
    .D(xor_1_out), .clk(xnor_1_out), .Q(d_ff_2_q), .Qn(d_ff_2_qn), .reset(and_26_out));  // open: preset
  xnor xnor_1 (xnor_1_out, or_1_out, or_3_out);
  and and_11 (and_11_out, not_3_out, not_4_out);
  not not_3 (not_3_out, or_4_out);
  not not_4 (not_4_out, d_ff_1_q);
  nor nor_1 (nor_1_out, d_ff_8_q, d_ff_5_q, d_ff_15_q, d_ff_16_q, not_9_out, not_10_out, not_8_out, not_5_out);
  or or_4 (or_4_out, d_ff_8_q, d_ff_5_q, d_ff_15_q, d_ff_16_q, d_ff_14_q, not_6_out, d_ff_11_q, d_ff_17_q);
  or or_5 (or_5_out, button_5_out, button_6_out);
  and and_12 (and_12_out, and_4_out, not_2_out);
  not not_5 (not_5_out, d_ff_2_q);
  not not_6 (not_6_out, d_ff_2_q);
  not not_7 (not_7_out, and_12_out);
  or or_6 (or_6_out, and_4_out, and_5_out);
  and and_13 (and_13_out, d_ff_1_q, d_ff_2_q);
  and and_14 (and_14_out, not_1_out, d_ff_2_qn);
  not not_8 (not_8_out, d_ff_11_q);
  not not_9 (not_9_out, d_ff_14_q);
  J_K_Flip_Flop j_k_ff_1 (
    .J(or_5_out), .K(button_6_out), .clk(or_5_out), .Q(j_k_ff_1_q), .Qn(j_k_ff_1_qn));  // open: preset, reset
  and and_15 (and_15_out, and_12_out, in_2);
  or or_7 (or_7_out, and_15_out, and_16_out);
  or or_8 (or_8_out, and_13_out, and_14_out);
  not not_10 (not_10_out, d_ff_17_q);
  and and_16 (and_16_out, not_7_out, d_ff_4_q);
  D_Flip_Flop #(.trigger("falling")) d_ff_3 (.D(or_7_out), .clk(or_6_out), .Q(d_ff_3_q));  // open: Qn, preset, reset
  xor xor_2 (xor_2_out, or_8_out, d_ff_5_q);
  and and_17 (and_17_out, not_7_out, d_ff_6_q);
  and and_18 (and_18_out, and_12_out, d_ff_3_q);
  or or_9 (or_9_out, and_18_out, and_17_out);
  D_Flip_Flop #(.trigger("falling")) d_ff_4 (.D(or_9_out), .clk(or_6_out), .Q(d_ff_4_q));  // open: Qn, preset, reset
  D_Flip_Flop d_ff_5 (
    .D(xor_2_out), .clk(xnor_1_out), .Q(d_ff_5_q), .Qn(d_ff_5_qn), .reset(or_12_out));  // open: preset
  and and_19 (and_19_out, and_12_out, d_ff_4_q);
  and and_20 (and_20_out, and_13_out, d_ff_5_q);
  and and_21 (and_21_out, d_ff_5_qn, and_14_out);
  and and_22 (and_22_out, d_ff_2_q, d_ff_5_q, d_ff_8_q, d_ff_11_q);
  and and_23 (and_23_out, not_7_out, d_ff_7_q);
  or or_10 (or_10_out, and_19_out, and_23_out);
  D_Flip_Flop #(.trigger("falling")) d_ff_6 (.D(or_10_out), .clk(or_6_out), .Q(d_ff_6_q));  // open: Qn, preset, reset
  or or_11 (or_11_out, and_20_out, and_21_out);
  or or_12 (or_12_out, and_22_out, and_26_out);
  and and_24 (and_24_out, and_12_out, d_ff_6_q);
  or or_13 (or_13_out, and_24_out, and_25_out);
  not not_11 (not_11_out, d_ff_2_q);
  and and_25 (and_25_out, not_7_out, d_ff_9_q);
  D_Flip_Flop #(.trigger("falling")) d_ff_7 (.D(or_13_out), .clk(or_6_out), .Q(d_ff_7_q));  // open: Qn, preset, reset
  xor xor_3 (xor_3_out, or_11_out, d_ff_8_q);
  D_Flip_Flop d_ff_8 (
    .D(xor_3_out), .clk(xnor_1_out), .Q(d_ff_8_q), .Qn(d_ff_8_qn), .reset(or_12_out));  // open: preset
  and and_26 (and_26_out, and_27_out, d_ff_1_q);
  and and_27 (and_27_out, not_11_out, d_ff_5_q, not_12_out, d_ff_11_q);
  not not_12 (not_12_out, d_ff_8_q);
  and and_28 (and_28_out, and_12_out, d_ff_7_q);
  or or_14 (or_14_out, and_28_out, and_31_out);
  and and_29 (and_29_out, and_20_out, d_ff_8_q);
  and and_30 (and_30_out, d_ff_8_qn, and_21_out);
  and and_31 (and_31_out, not_7_out, d_ff_10_q);
  D_Flip_Flop #(.trigger("falling")) d_ff_9 (.D(or_14_out), .clk(or_6_out), .Q(d_ff_9_q));  // open: Qn, preset, reset
  and and_32 (and_32_out, d_ff_2_q, not_14_out, not_13_out, d_ff_11_q);
  not not_13 (not_13_out, d_ff_8_q);
  not not_14 (not_14_out, d_ff_5_q);
  or or_15 (or_15_out, and_29_out, and_30_out);
  and and_33 (and_33_out, not_7_out, d_ff_12_q);
  and and_34 (and_34_out, and_12_out, d_ff_9_q);
  or or_16 (or_16_out, and_34_out, and_33_out);
  D_Flip_Flop #(.trigger("falling")) d_ff_10 (.D(or_16_out), .clk(or_6_out), .Q(d_ff_10_q));  // open: Qn, preset, reset
  xor xor_4 (xor_4_out, or_15_out, d_ff_11_q);
  and and_35 (and_35_out, d_ff_1_q, and_32_out);
  and and_36 (and_36_out, and_12_out, d_ff_10_q);
  D_Flip_Flop d_ff_11 (
    .D(xor_4_out), .clk(xnor_1_out), .Q(d_ff_11_q), .Qn(d_ff_11_qn), .reset(and_26_out));  // open: preset
  and and_37 (and_37_out, not_7_out, d_ff_13_q);
  or or_17 (or_17_out, and_36_out, and_37_out);
  D_Flip_Flop #(.trigger("falling")) d_ff_12 (.D(or_17_out), .clk(or_6_out), .Q(d_ff_12_q));  // open: Qn, preset, reset
  and and_38 (and_38_out, and_29_out, d_ff_11_q);
  and and_39 (and_39_out, d_ff_11_qn, and_30_out);
  or or_18 (or_18_out, and_38_out, and_35_out);
  and and_40 (and_40_out, and_12_out, d_ff_12_q);
  or or_19 (or_19_out, and_40_out, and_41_out);
  and and_41 (and_41_out, not_7_out, in_3);
  D_Flip_Flop #(.trigger("falling")) d_ff_13 (.D(or_19_out), .clk(or_6_out), .Q(d_ff_13_q));  // open: Qn, preset, reset
  or or_20 (or_20_out, or_18_out, and_39_out);
  and and_42 (and_42_out[0], ON_OFF, d_ff_14_q);
  and and_43 (and_42_out[1], ON_OFF, d_ff_15_q);
  and and_44 (and_42_out[2], ON_OFF, d_ff_16_q);
  and and_45 (and_42_out[3], ON_OFF, d_ff_17_q);
  xor xor_5 (xor_5_out, or_20_out, d_ff_14_q);
  D_Flip_Flop d_ff_14 (
    .D(xor_5_out), .clk(xnor_1_out), .Q(d_ff_14_q), .Qn(d_ff_14_qn), .reset(and_61_out));  // open: preset
  and and_46 (and_46_out, ON_OFF, j_k_ff_1_q);
  and and_47 (and_47_out, j_k_ff_1_qn, ON_OFF);
  and and_48 (and_48_out, ON_OFF, d_ff_13_q);
  LED led_1 (.in(and_48_out));
  and and_49 (and_49_out, ON_OFF, d_ff_12_q);
  LED led_2 (.in(and_49_out));
  and and_50 (and_50_out, ON_OFF, d_ff_10_q);
  LED led_3 (.in(and_50_out));
  LED led_4 (.in(and_51_out));
  and and_51 (and_51_out, ON_OFF, d_ff_9_q);
  and and_52 (and_52_out, ON_OFF, d_ff_7_q);
  LED led_5 (.in(and_52_out));
  LED led_6 (.in(and_53_out));
  and and_53 (and_53_out, ON_OFF, d_ff_6_q);
  and and_54 (and_54_out, ON_OFF, d_ff_4_q);
  LED led_7 (.in(and_54_out));
  LED led_8 (.in(and_55_out));
  and and_55 (and_55_out, ON_OFF, d_ff_3_q);
  and and_56 (and_56_out, or_18_out, d_ff_14_q);
  and and_57 (and_57_out, d_ff_14_qn, and_39_out);
  LED led_9 (.in(and_46_out));
  LED led_10 (.in(and_47_out));
  or or_21 (or_21_out, and_56_out, and_57_out);
  xor xor_6 (xor_6_out, or_21_out, d_ff_15_q);
  D_Flip_Flop d_ff_15 (
    .D(xor_6_out), .clk(xnor_1_out), .Q(d_ff_15_q), .Qn(d_ff_15_qn), .reset(or_23_out));  // open: preset
  and and_58 (and_58_out, and_56_out, d_ff_15_q);
  and and_59 (and_59_out, d_ff_15_qn, and_57_out);
  and and_60 (and_60_out, d_ff_14_q, d_ff_15_q, d_ff_16_q, d_ff_17_q);
  or or_22 (or_22_out, and_58_out, and_59_out);
  or or_23 (or_23_out, and_60_out, and_61_out);
  xor xor_7 (xor_7_out, or_22_out, d_ff_16_q);
  and and_61 (and_61_out, and_62_out, d_ff_1_q);
  and and_62 (and_62_out, not_16_out, d_ff_15_q, not_15_out, d_ff_17_q);
  not not_15 (not_15_out, d_ff_16_q);
  not not_16 (not_16_out, d_ff_14_q);
  D_Flip_Flop d_ff_16 (
    .D(xor_7_out), .clk(xnor_1_out), .Q(d_ff_16_q), .Qn(d_ff_16_qn), .reset(or_23_out));  // open: preset
  and and_63 (and_63_out, and_58_out, d_ff_16_q);
  and and_64 (and_64_out, d_ff_16_qn, and_59_out);
  or or_24 (or_24_out, and_63_out, and_64_out);
  xor xor_8 (xor_8_out, or_24_out, d_ff_17_q);
  D_Flip_Flop d_ff_17 (.D(xor_8_out), .clk(xnor_1_out), .Q(d_ff_17_q), .reset(and_61_out));  // open: Qn, preset
  Button button_7 ();  // open: out
  LED led_11 ();  // open: in

  // Notes on the sheet:
  //   PREVIOUS
  //   NEXT
  //   VOL +
  //   VOL -
  //   PLAY
  //   PAUSE
  //   PLAY
  //   PAUSE
endmodule
