// Logisim project countdown.circ as structural Verilog: 1 circuit, main circuit main
module main (
  input  in_1
);

  wire and_1_out, and_2_out, button_1_out, j_k_ff_1_qn, j_k_ff_2_qn, j_k_ff_3_qn, j_k_ff_4_qn;
  wire [3:0] j_k_ff_1_q;

  Button button_1 (.out(button_1_out));
  J_K_Flip_Flop #(.trigger("falling")) j_k_ff_1 (
    .J(in_1), .clk(button_1_out), .K(in_1), .Q(j_k_ff_1_q[0]), .Qn(j_k_ff_1_qn));  // open: preset, en, reset
  J_K_Flip_Flop #(.trigger("falling")) j_k_ff_2 (
    .J(in_1), .clk(j_k_ff_1_qn), .K(in_1), .Q(j_k_ff_1_q[1]), .Qn(j_k_ff_2_qn), .reset(and_2_out));  // open: preset, en
  J_K_Flip_Flop #(.trigger("falling")) j_k_ff_3 (
    .J(in_1), .clk(j_k_ff_2_qn), .K(in_1), .Q(j_k_ff_1_q[2]), .Qn(j_k_ff_3_qn), .reset(and_2_out));  // open: preset, en
  J_K_Flip_Flop #(.trigger("falling")) j_k_ff_4 (
    .J(in_1), .clk(j_k_ff_3_qn), .K(in_1), .Q(j_k_ff_1_q[3]), .Qn(j_k_ff_4_qn));  // open: preset, en, reset
  and and_1 (and_1_out, j_k_ff_1_q[0], j_k_ff_1_q[1], j_k_ff_1_q[2], j_k_ff_4_qn);
  and and_2 (and_2_out, and_1_out, j_k_ff_1_q[3]);
  Hex_Digit_Display hex_digit_display_1 (.value(j_k_ff_1_q));  // open: dp
endmodule
