// Logisim project errror.circ as structural Verilog: 1 circuit, main circuit main
module main (
  input  in_1
);

  wire and_1_out, clock_1_out;
  wire [3:0] j_k_ff_1_q;

  Clock clock_1 (.out(clock_1_out));
  J_K_Flip_Flop j_k_ff_1 (.J(in_1), .K(in_1), .clk(clock_1_out), .Q(j_k_ff_1_q[0]));  // open: Qn, preset, reset
  J_K_Flip_Flop j_k_ff_2 (
    .J(in_1), .K(in_1), .clk(j_k_ff_1_q[0]), .Q(j_k_ff_1_q[1]), .reset(and_1_out));  // open: Qn, preset
  J_K_Flip_Flop j_k_ff_3 (
    .J(in_1), .K(in_1), .clk(j_k_ff_1_q[1]), .Q(j_k_ff_1_q[2]), .reset(and_1_out));  // open: Qn, preset
  J_K_Flip_Flop j_k_ff_4 (.J(in_1), .K(in_1), .clk(j_k_ff_1_q[2]), .Q(j_k_ff_1_q[3]));  // open: Qn, preset, reset
  and and_1 (and_1_out, j_k_ff_1_q[1], j_k_ff_1_q[0], j_k_ff_1_q[2], j_k_ff_1_q[3]);
  LED led_1 (.in(and_1_out));
  Hex_Digit_Display hex_digit_display_1 (.value(j_k_ff_1_q));  // open: dp
endmodule
