// Logisim project fullconnection.circ as structural Verilog: 1 circuit, main circuit main
module main (
  input  in_1,
  input  in_2,
  input  in_3,
  input  in_4,
  input  in_5
);

  wire and_1_out, and_2_out, and_3_out, clock_1_out, not_1_out, or_1_out, or_2_out;

  not not_1 (not_1_out, in_1);
  Clock clock_1 (.out(clock_1_out));
  and and_1 (and_1_out, in_1, in_2);
  and and_2 (and_2_out, in_2, not_1_out);
  D_Flip_Flop d_ff_1 (.D(or_1_out), .clk(clock_1_out), .reset(in_5));  // open: Q, Qn, preset
  or or_1 (or_1_out, and_3_out, and_2_out);
  buf or_2 (or_2_out, and_1_out);  // OR_Gate
  D_Flip_Flop d_ff_2 (.D(or_2_out), .clk(clock_1_out), .reset(in_5));  // open: Q, Qn, preset
  buf and_3 (and_3_out, in_1);  // AND_Gate
  // AND_Gate and_4 has open pins: in1=not_1_out, out=open

  // Notes on the sheet:
  //   R-L
  //   L-R
  //   R-L
  //   L-R
endmodule
