// Logisim project track0_99.circ as structural Verilog: 1 circuit, main circuit main
module main (
);

  wire and_1_out, and_2_out, and_3_out, and_4_out, and_5_out, and_6_out, and_7_out, and_8_out, and_9_out,
       and_10_out, and_11_out, and_12_out, and_13_out, and_14_out, and_15_out, and_16_out, and_17_out,
       and_18_out, and_19_out, and_20_out, and_21_out, and_22_out, and_23_out, button_1_out, button_2_out,
       d_ff_1_q, d_ff_2_qn, d_ff_3_qn, d_ff_4_qn, d_ff_5_qn, d_ff_6_qn, d_ff_7_qn, d_ff_8_qn, not_1_out,
       not_2_out, not_3_out, not_4_out, not_5_out, not_6_out, not_7_out, or_1_out, or_2_out, or_3_out,
       or_4_out, or_5_out, or_6_out, or_7_out, or_8_out, or_9_out, or_10_out, or_11_out, or_12_out,
       xor_1_out, xor_2_out, xor_3_out, xor_4_out, xor_5_out, xor_6_out, xor_7_out, xor_8_out;
  wire [3:0] d_ff_2_q, d_ff_6_q;

  Button button_1 (.out(button_1_out));
  Button button_2 (.out(button_2_out));
  and and_1 (and_1_out, button_1_out, button_1_out);
  D_Flip_Flop d_ff_1 (.D(button_2_out), .clk(button_2_out), .Q(d_ff_1_q), .reset(and_1_out));  // open: Qn, preset
  or or_1 (or_1_out, button_1_out, button_2_out);
  Hex_Digit_Display hex_digit_display_1 (.value(d_ff_6_q));  // open: dp
  Hex_Digit_Display hex_digit_display_2 (.value(d_ff_2_q));  // open: dp
  not not_1 (not_1_out, d_ff_1_q);
  or or_2 (or_2_out, d_ff_1_q, not_1_out);
  xor xor_1 (xor_1_out, or_2_out, d_ff_2_q[0]);
  D_Flip_Flop #(.trigger("falling")) d_ff_2 (
    .D(xor_1_out), .clk(or_1_out), .Q(d_ff_2_q[0]), .Qn(d_ff_2_qn), .reset(and_7_out));  // open: preset
  and and_2 (and_2_out, d_ff_1_q, d_ff_2_q[0]);
  and and_3 (and_3_out, not_1_out, d_ff_2_qn);
  or or_3 (or_3_out, and_2_out, and_3_out);
  xor xor_2 (xor_2_out, or_3_out, d_ff_2_q[1]);
  D_Flip_Flop #(.trigger("falling")) d_ff_3 (
    .D(xor_2_out), .clk(or_1_out), .Q(d_ff_2_q[1]), .Qn(d_ff_3_qn), .reset(or_5_out));  // open: preset
  and and_4 (and_4_out, and_2_out, d_ff_2_q[1]);
  and and_5 (and_5_out, d_ff_3_qn, and_3_out);
  and and_6 (and_6_out, d_ff_2_q[0], d_ff_2_q[1], d_ff_2_q[2], d_ff_2_q[3]);
  or or_4 (or_4_out, and_4_out, and_5_out);
  or or_5 (or_5_out, and_6_out, and_7_out);
  xor xor_3 (xor_3_out, or_4_out, d_ff_2_q[2]);
  and and_7 (and_7_out, and_8_out, d_ff_1_q);
  and and_8 (and_8_out, not_2_out, d_ff_2_q[1], not_3_out, d_ff_2_q[3]);
  not not_2 (not_2_out, d_ff_2_q[0]);
  not not_3 (not_3_out, d_ff_2_q[2]);
  D_Flip_Flop #(.trigger("falling")) d_ff_4 (
    .D(xor_3_out), .clk(or_1_out), .Q(d_ff_2_q[2]), .Qn(d_ff_4_qn), .reset(or_5_out));  // open: preset
  and and_9 (and_9_out, and_4_out, d_ff_2_q[2]);
  and and_10 (and_10_out, d_ff_4_qn, and_5_out);
  and and_11 (and_11_out, d_ff_2_q[0], not_4_out, not_5_out, d_ff_2_q[3]);
  not not_4 (not_4_out, d_ff_2_q[1]);
  not not_5 (not_5_out, d_ff_2_q[2]);
  or or_6 (or_6_out, and_9_out, and_10_out);
  xor xor_4 (xor_4_out, or_6_out, d_ff_2_q[3]);
  and and_12 (and_12_out, d_ff_1_q, and_11_out);
  D_Flip_Flop #(.trigger("falling")) d_ff_5 (
    .D(xor_4_out), .clk(or_1_out), .Q(d_ff_2_q[3]), .Qn(d_ff_5_qn), .reset(and_7_out));  // open: preset
  and and_13 (and_13_out, and_9_out, d_ff_2_q[3]);
  and and_14 (and_14_out, d_ff_5_qn, and_10_out);
  or or_7 (or_7_out, and_13_out, and_12_out);
  or or_8 (or_8_out, or_7_out, and_14_out);
  xor xor_5 (xor_5_out, or_8_out, d_ff_6_q[0]);
  D_Flip_Flop #(.trigger("falling")) d_ff_6 (
    .D(xor_5_out), .clk(or_1_out), .Q(d_ff_6_q[0]), .Qn(d_ff_6_qn), .reset(and_21_out));  // open: preset
  and and_15 (and_15_out, or_7_out, d_ff_6_q[0]);
  and and_16 (and_16_out, d_ff_6_qn, and_14_out);
  or or_9 (or_9_out, and_15_out, and_16_out);
  xor xor_6 (xor_6_out, or_9_out, d_ff_6_q[1]);
  D_Flip_Flop #(.trigger("falling")) d_ff_7 (
    .D(xor_6_out), .clk(or_1_out), .Q(d_ff_6_q[1]), .Qn(d_ff_7_qn), .reset(or_10_out));  // open: preset
  and and_17 (and_17_out, and_15_out, d_ff_6_q[1]);
  and and_18 (and_18_out, d_ff_7_qn, and_16_out);
  and and_19 (and_19_out, d_ff_6_q[0], d_ff_6_q[1], d_ff_6_q[2], d_ff_6_q[3]);
  or or_10 (or_10_out, and_19_out, and_21_out);
  or or_11 (or_11_out, and_17_out, and_18_out);
  Button button_3 ();  // open: out
  xor xor_7 (xor_7_out, or_11_out, d_ff_6_q[2]);
  and and_20 (and_20_out, not_6_out, d_ff_6_q[1], not_7_out, d_ff_6_q[3]);
  not not_6 (not_6_out, d_ff_6_q[0]);
  not not_7 (not_7_out, d_ff_6_q[2]);
  D_Flip_Flop #(.trigger("falling")) d_ff_8 (
    .D(xor_7_out), .clk(or_1_out), .Q(d_ff_6_q[2]), .Qn(d_ff_8_qn), .reset(or_10_out));  // open: preset
  and and_21 (and_21_out, and_20_out, d_ff_1_q);
  and and_22 (and_22_out, and_17_out, d_ff_6_q[2]);
  and and_23 (and_23_out, d_ff_8_qn, and_18_out);
  or or_12 (or_12_out, and_22_out, and_23_out);
  xor xor_8 (xor_8_out, or_12_out, d_ff_6_q[3]);
  D_Flip_Flop #(.trigger("falling")) d_ff_9 (
    .D(xor_8_out), .clk(or_1_out), .Q(d_ff_6_q[3]), .reset(and_21_out));  // open: Qn, preset
  LED led_1 ();  // open: in
endmodule
